# Fritzing sketch connectionDiagramVccToThermistor (saved by Fritzing 0.9.3b)
breadboards: 1

parts:
  Componente1 = Arduino Uno (Rev3)
  R1 = Resistor [tolerance=±5% resistance=10k package=THT]
  R2 = Temperature Sensor (Thermistor) [thermistor_type=NTC package=THT]

nets:
  N1: Componente1.A3, R1.Pin_1, R2.pin_0
  N2: Componente1.5V, R2.pin_1
  N3: Componente1.GND, R1.Pin_0
